# Fritzing sketch circuit (saved by Fritzing 0.9.3b)
breadboards: 2

parts:
  부품1 = Arduino Uno (Rev3)
  부품2 = Arduino Uno (Rev3)
  R1 = Resistor [tolerance=±5% resistance=220 package=THT]  # not connected
  R2 = Resistor [tolerance=±5% resistance=220 package=THT]
  R3 = Resistor [tolerance=±5% resistance=220 package=THT]
  R4 = Resistor [tolerance=±5% resistance=220 package=THT]
  J1 = Basic Servo
  J2 = Basic Servo
  J3 = Basic Servo  # not connected
  J4 = Basic Servo
  R5 = Photocell (LDR) [package=THT]
  R6 = Photocell (LDR) [package=THT]
  R7 = Photocell (LDR) [package=THT]
  R8 = Photocell (LDR) [package=THT]

nets:
  N1: 부품1.A4/SDA, R2.Pin_1
  N2: 부품1.A5/SCL, R5.pin_0
  N3: 부품1.D1/TX, J4.pulse
  N4: 부품1.5V, R5.pin_1, R6.pin_1, R7.pin_1, R8.pin_1
  N5: 부품1.GND, R2.Pin_0
  N6: 부품2.A4/SDA, R3.Pin_1, R8.pin_0
  N7: 부품2.A5/SCL, R4.Pin_1, R7.pin_0
  N8: 부품2.D3_PWM, J2.pulse
  N9: 부품2.D4, J1.pulse
  5V: 부품2.5V, J1.vcc
  N10: 부품2.GND, R3.Pin_0, R4.Pin_0
